# Fritzing sketch wiring (saved by Fritzing 0.9.2b)
breadboards: 1

parts:
  R1 = Resistor [tolerance=±5% resistance=10k package=THT]
  DHT11 = DHT11 Humitidy and Temperature Sensor
  S1 = SWITCH-MOMENTARY-2 [package=tactile-switch-1101ne]
  S2 = SWITCH-MOMENTARY-2 [package=tactile-switch-1101ne]
  D1 = Diode [package=diode-1n4001]
  J1 = Screw terminal - 2 pins [package=THT]
  J2 = Screw terminal - 2 pins [package=THT]
  U1 = ESP8266 WiFi Module [part_number=ESP8266]
  IC1 = V_REG_LD1117VXX [package=78xxl]
  Q2 = NPN-Transistor [package="TO92 [THT]"]
  R3 = Resistor [tolerance=±5% resistance=33 package=THT]
  R4 = Resistor [tolerance=±5% resistance=100 package=THT]
  R5 = Resistor [tolerance=±5% resistance=100 package=THT]
  Q1 = Basic FET N-Channel [package="TO220 [THT]"]
  Cout = Electrolytic Capacitor [capacitance=10µF voltage=20V package="1010 [SMD, electrolytic]"]
  R6 = Resistor [tolerance=±5% resistance=1k package=THT]
  R7 = Resistor [tolerance=±5% resistance=1k package=THT]
  Cin = Electrolytic Capacitor [capacitance=100nF voltage=20V package="1010 [SMD, electrolytic]"]

nets:
  N1: R1.Pin_0, DHT11.DATA, U1.GPIO_0
  VDD: R1.Pin_1, DHT11.VDD, U1.VCC, IC1.OUT, R4.Pin_0, R5.Pin_1, Cout.+, R6.Pin_0, R7.Pin_0
  GND: DHT11.GND, J1.pin2, U1.GND, IC1.GND, R3.Pin_0, Q1.source, Cout.-, Cin.-
  N2: S1.1, S2.1, Q2.B, Q1.gate
  N3: S1.2, S2.2, R4.Pin_1
  N4: D1.A, J1.pin1
  N5: D1.C, J2.pin2, IC1.IN, Cin.+
  N6: J2.pin1, Q1.drain
  N7: U1.RST, R7.Pin_1
  N8: U1.GPIO_2, Q2.C, R5.Pin_0
  N9: U1.CH_PD, R6.Pin_1
  N10: Q2.E, R3.Pin_1

notes:
  + 12V input DC -->
  GND input -->
  <-- GND output
  <-- + 12V LEDs output
  GND input -->
  + 12V input DC -->
  G
  D
  S
  12V -->
  3.3V -->

custom parts:
  DHT11 Humitidy and Temperature Sensor: DHT11 Humidity and Temperature Sensor
  ESP8266 WiFi Module: Generic WiFi Module based on the ESP8266 with onboard PCB antenna and UART communications
